# Fritzing sketch wifi_回路図 (saved by Fritzing 0.9.5d)
circuit board: 8.00706cm x 7.42333cm
breadboards: 1

parts:
  Raspberry_Pi_1 = Raspberry Pi 3 [part_number=RPI-3-V1.2]
  M1 = DC Motor
  M2 = DC Motor
  パーツ1 = Triple Axis Magnetometer - HMC5883 Breakout
  IC1 = L293D [package=THT]
  VCC1 = 4 x AAA Battery Mount
  V1 = DC Power [voltage=3.3V]
  C2 = Ceramic Capacitor [capacitance=100nF voltage=35V package="100 mil [THT, multilayer]"]
  VCC2 = Battery block 9V
  C3 = Ceramic Capacitor [capacitance=100nF voltage=35V package="100 mil [THT, multilayer]"]
  C1 = Ceramic Capacitor [capacitance=100nF voltage=35V package="100 mil [THT, multilayer]"]
  J1 = female pin header, 2 pins [form="♀ (female)"]
  R1 = Resistor [tolerance=±5% resistance=1000 package=THT]
  R2 = Resistor [tolerance=±5% resistance=1000 package=THT]
  J2 = female pin header, 1 pin [form="♀ (female)"]  # not connected
  J3 = female pin header, 1 pin [form="♀ (female)"]  # not connected
  J4 = female pin header, 1 pin [form="♀ (female)"]  # not connected
  J5 = female pin header, 1 pin [form="♀ (female)"]  # not connected
  J6 = female pin header, 1 pin [form="♀ (female)"]  # not connected
  J7 = female pin header, 1 pin [form="♀ (female)"]  # not connected
  J8 = female pin header, 1 pin [form="♀ (female)"]  # not connected
  J9 = female pin header, 1 pin [form="♀ (female)"]  # not connected
  J10 = female pin header, 1 pin [form="♀ (female)"]  # not connected
  J11 = female pin header, 1 pin [form="♀ (female)"]  # not connected
  J12 = female pin header, 1 pin [form="♀ (female)"]  # not connected
  J13 = female pin header, 1 pin [form="♀ (female)"]  # not connected
  M3 = NEO-6M GPS Module [part_number=GY-GPS6MV2]

nets:
  N1: Raspberry_Pi_1.GPIO2, パーツ1.SCL
  N2: Raspberry_Pi_1.GPIO3, パーツ1.SDA
  N3: Raspberry_Pi_1.GIPO17, IC1.In_3
  N4: Raspberry_Pi_1.GIPO27, IC1.In_4
  N5: Raspberry_Pi_1.GIPO22, R1.Pin_1
  N6: Raspberry_Pi_1.GIPO5, IC1.In_2
  N7: Raspberry_Pi_1.GIPO6, IC1.In_1
  N8: Raspberry_Pi_1.GIPO13, R2.Pin_1
  GND: Raspberry_Pi_1.GND, パーツ1.GND, IC1.0V, VCC1.-, V1.V-, C2.0, VCC2.-, C3.0, C1.0, J1.pin2, M3.GND
  N9: Raspberry_Pi_1.GIPO15, M3.Rx
  N10: Raspberry_Pi_1.GIPO14, M3.Tx
  N11: M1.pin_1, IC1.Out_3_(_Controlled_by_Enable_2_)
  N12: M1.pin_2, IC1.Out_4_(_Controlled_by_Enable_2_)
  N13: M2.pin_1, IC1.Out_2_(_Controlled_by_Enable_1_)
  N14: M2.pin_2, IC1.Out_1_(_Controlled_by_Enable_1_)
  vcc_3v: パーツ1.VCC, V1.V+, C2.1
  N15: IC1.Enable_1, R2.Pin_0
  vcc_9v: IC1.+Vmotor, VCC2.+, C3.1
  N16: IC1.Enable_2, R1.Pin_0
  vcc_5v: IC1.+V, VCC1.+, C1.1, J1.pin1, M3.Vcc

custom parts:
  NEO-6M GPS Module: GY-GPS6MV2 NEO-6M GPS Module Module based on U-blox NEO-6M GPS engine, incorporating regulator for 3.3-5V DC input, MS621FE-compatible rechargeable battery for backup and EEPROM for storing configuration settings. Links: NEO-6 series product information page NEO-6 Datasheet
